# Fritzing sketch design (saved by Fritzing 0.9.3b)

parts:
  A1 = Waveshare rp2040-zero tht [package=THT]
  NEOPIXEL1 = Neopixel Strip -- Black (30/m)
  R1 = Rotary Potentiometer (Small) [maximum_resistance=100kΩ package=THT]
  S1 = Round Pushbutton
  SP1 = SPEAKER [package=pcb_mount_speaker]

nets:
  N1: A1.Pin_2, S1.leg0, SP1.+
  N2: A1.Pin_3, NEOPIXEL1.+5V, R1.leg2
  N3: A1.Pin_9, R1.wiper
  N4: A1.Pin_18, S1.leg1
  N5: A1.Pin_20, SP1.-
  N6: NEOPIXEL1.GND, R1.leg1

custom parts:
  Waveshare rp2040-zero tht: .RP2040-Zero, A Low-Cost, High-Performance Pico-Like MCU Board Based On Raspberry Pi Microcontroller RP2040. This varant is THT without the extra connections.
  Neopixel Strip -- Black (30/m): Neopixel Strip, Black, 30 pixels per meter.
