# Fritzing sketch design2 (saved by Fritzing 0.9.3b)
breadboards: 1

parts:
  A2 = Waveshare rp2040-zero tht [package=THT]
  R2 = Rotary Potentiometer (Small) [maximum_resistance=100kΩ package=THT]
  S2 = Round Pushbutton
  SP2 = SPEAKER [package=pcb_mount_speaker]
  NEOPIXEL2 = Neopixel Strip -- Black (30/m)

nets:
  N1: A2.Pin_1, NEOPIXEL2.+5V
  N2: A2.Pin_2, R2.leg1, S2.leg1, SP2.+, NEOPIXEL2.GND
  N3: A2.Pin_3, R2.leg2
  N4: A2.Pin_7, R2.wiper
  N5: A2.Pin_9, NEOPIXEL2.DI
  N6: A2.Pin_17, S2.leg0
  N7: A2.Pin_21, SP2.-

custom parts:
  Waveshare rp2040-zero tht: .RP2040-Zero, A Low-Cost, High-Performance Pico-Like MCU Board Based On Raspberry Pi Microcontroller RP2040. This varant is THT without the extra connections.
  Neopixel Strip -- Black (30/m): Neopixel Strip, Black, 30 pixels per meter.
