# Fritzing sketch pcb_001 (saved by Fritzing 0.9.3b)
circuit board: 4cm x 3.7cm
breadboards: 1

parts:
  A1 = Waveshare rp2040-zero tht [package=THT]
  U1 = LM 358 Dual Op-Amp [package="DIP8 [THT]"]
  J1 = female pin header, 3 pins [form="♀ (female)"]
  J2 = female pin header, 3 pins [form="♀ (female)"]
  J3 = female pin header, 2 pins [form="♀ (female)"]
  J4 = female pin header, 2 pins [form="♀ (female)"]

nets:
  N1: A1.Pin_1, U1.connector3, J1.pin1
  N2: A1.Pin_2, U1.connector7, J1.pin2, J2.pin1, J3.pin2, J4.pin1
  N3: A1.Pin_3, J2.pin3
  N4: A1.Pin_6, J1.pin3
  N5: A1.Pin_7, J2.pin2
  N6: A1.Pin_15, U1.connector6
  N7: A1.Pin_18, J3.pin1
  N8: U1.connector4, U1.connector5, J4.pin2

custom parts:
  Waveshare rp2040-zero tht: .RP2040-Zero, A Low-Cost, High-Performance Pico-Like MCU Board Based On Raspberry Pi Microcontroller RP2040. This varant is THT without the extra connections.
